// Logisim project P1_P2_Combinational.circ as structural Verilog: 14 circuits, main circuit main
module main (
  input  in_1,
  input  in_2,
  output out_3
);

  wire nand_1_out;

  nand nand_1 (nand_1_out, in_1, in_2);
  nand nand_2 (out_3, nand_1_out, nand_1_out);
endmodule

module Impl_OR (
  input  In1,
  input  In2,
  input  in_3,
  input  in_4,
  output Out1,
  output out_6
);

  wire and_1_out, nand_1_out, nand_2_out, not_1_out, not_2_out;

  nand nand_1 (nand_1_out, 1'b1, In1);
  nand nand_2 (nand_2_out, 1'b1, In2);
  not not_1 (not_1_out, in_3);
  not not_2 (not_2_out, in_4);
  and and_1 (and_1_out, not_1_out, not_2_out);
  nand nand_3 (Out1, nand_1_out, nand_2_out);
  not not_3 (out_6, and_1_out);
endmodule

module Impl_XOR (
  input  In1,
  input  In2,
  input  in_3,
  input  in_4,
  output Out1,
  output out_6
);

  wire and_1_out, nand_1_out, nand_2_out, nand_3_out, nand_4_out, not_1_out, or_1_out;

  nand nand_1 (nand_1_out, 1'b1, In1);
  nand nand_2 (nand_2_out, 1'b1, In2);
  or or_1 (or_1_out, in_3, in_4);
  and and_1 (and_1_out, in_3, in_4);
  not not_1 (not_1_out, and_1_out);
  nand nand_3 (nand_3_out, nand_1_out, In2);
  nand nand_4 (nand_4_out, In1, nand_2_out);
  and and_2 (out_6, or_1_out, not_1_out);
  nand nand_5 (Out1, nand_3_out, nand_4_out);
endmodule

module Impl_NOT (
  input  In1,
  output Out1
);

  nand nand_1 (Out1, 1'b1, In1);
endmodule

module Impl_Mux_Demux (
  input  a_m,
  input  b_m,
  input  sel_m,
  input  in_d,
  input  sel_d,
  output out_m,
  output a_d,
  output b_d
);

  wire and_1_out, and_2_out, not_1_out, not_2_out;

  not not_1 (not_1_out, sel_m);
  not not_2 (not_2_out, sel_d);
  and and_1 (and_1_out, not_1_out, a_m);
  and and_2 (and_2_out, b_m, sel_m);
  and and_3 (a_d, not_2_out, in_d);
  and and_4 (b_d, sel_d, in_d);
  or or_1 (out_m, and_1_out, and_2_out);
endmodule

module Impl_Mux4Way16 (
  input  a,
  input  b,
  input  c,
  input  d,
  input  sel_0,
  input  sel_1,
  output out_m16
);

  wire multiplexer_1_out, multiplexer_2_out;

  Multiplexer multiplexer_1 (.in0(a), .in1(b), .out(multiplexer_1_out), .sel(sel_0));
  Multiplexer multiplexer_2 (.in0(c), .in1(d), .out(multiplexer_2_out), .sel(sel_0));
  Multiplexer multiplexer_3 (.in0(multiplexer_1_out), .in1(multiplexer_2_out), .out(out_m16), .sel(sel_1));
endmodule

module Impl_Demux4Way (
  input  d_in,
  input  sel_1,
  input  sel_0,
  output a,
  output b,
  output c,
  output d
);

  wire demultiplexer_2_out0, demultiplexer_2_out1;

  Demultiplexer demultiplexer_1 (.out0(a), .out1(b), .in(demultiplexer_2_out0), .sel(sel_0));
  Demultiplexer demultiplexer_2 (.out0(demultiplexer_2_out0), .out1(demultiplexer_2_out1), .in(d_in), .sel(sel_1));
  Demultiplexer demultiplexer_3 (.out0(c), .out1(d), .in(demultiplexer_2_out1), .sel(sel_0));
endmodule

module Impl_HalfAdder (
  input  a,
  input  b,
  output sum,
  output carry
);

  and and_1 (carry, a, b);
  xor xor_1 (sum, a, b);
endmodule

module Impl_FullAdder (
  input  a,
  input  b,
  input  c,
  input  a1,
  input  b1,
  input  c1,
  output sum,
  output carry,
  output sum1,
  output carry1
);

  wire and_1_out, and_2_out, impl_halfadder_1_carry, impl_halfadder_1_sum, impl_halfadder_2_carry, xor_1_out;

  xor xor_1 (xor_1_out, b, c);
  and and_1 (and_1_out, b, c);
  xor xor_2 (sum, a, xor_1_out);
  and and_2 (and_2_out, a, xor_1_out);
  Impl_HalfAdder impl_halfadder_1 (.a(b1), .b(c1), .sum(impl_halfadder_1_sum), .carry(impl_halfadder_1_carry));
  or or_1 (carry, and_2_out, and_1_out);
  Impl_HalfAdder impl_halfadder_2 (.a(a1), .b(impl_halfadder_1_sum), .sum(sum1), .carry(impl_halfadder_2_carry));
  or or_2 (carry1, impl_halfadder_2_carry, impl_halfadder_1_carry);
endmodule

module Impl_Add16 (
  input  a7,
  input  b7,
  input  a6,
  input  b6,
  input  a5,
  input  b5,
  input  a4,
  input  b4,
  input  a3,
  input  b3,
  input  a2,
  input  b2,
  input  a1,
  input  b1,
  input  a0,
  input  b0,
  output out7,
  output ov,
  output out6,
  output out5,
  output out4,
  output out3,
  output out2,
  output out1,
  output out0
);

  wire impl_fulladder_2_carry, impl_fulladder_3_carry, impl_fulladder_4_carry, impl_fulladder_5_carry,
       impl_fulladder_6_carry, impl_fulladder_7_carry, impl_fulladder_8_carry;

  Impl_FullAdder impl_fulladder_1 (
    .a(a7), .b(b7), .c(impl_fulladder_2_carry), .sum(out7), .carry(ov));  // open: a1, b1, c1, sum1, carry1
  Impl_FullAdder impl_fulladder_2 (
    .a(a6), .b(b6), .c(impl_fulladder_3_carry), .sum(out6), .carry(impl_fulladder_2_carry));  // open: a1, b1, c1, sum1, carry1
  Impl_FullAdder impl_fulladder_3 (
    .a(a5), .b(b5), .c(impl_fulladder_4_carry), .sum(out5), .carry(impl_fulladder_3_carry));  // open: a1, b1, c1, sum1, carry1
  Impl_FullAdder impl_fulladder_4 (
    .a(a4), .b(b4), .c(impl_fulladder_5_carry), .sum(out4), .carry(impl_fulladder_4_carry));  // open: a1, b1, c1, sum1, carry1
  Impl_FullAdder impl_fulladder_5 (
    .a(a3), .b(b3), .c(impl_fulladder_6_carry), .sum(out3), .carry(impl_fulladder_5_carry));  // open: a1, b1, c1, sum1, carry1
  Impl_FullAdder impl_fulladder_6 (
    .a(a2), .b(b2), .c(impl_fulladder_7_carry), .sum(out2), .carry(impl_fulladder_6_carry));  // open: a1, b1, c1, sum1, carry1
  Impl_FullAdder impl_fulladder_7 (
    .a(a1), .b(b1), .c(impl_fulladder_8_carry), .sum(out1), .carry(impl_fulladder_7_carry));  // open: a1, b1, c1, sum1, carry1
  Impl_FullAdder impl_fulladder_8 (
    .a(a0), .b(b0), .c(1'b0), .sum(out0), .carry(impl_fulladder_8_carry));  // open: a1, b1, c1, sum1, carry1
endmodule

module test_Add16 (
);

  wire dipswitch_1_sw1, dipswitch_1_sw2, dipswitch_1_sw3, dipswitch_1_sw4, dipswitch_1_sw5, dipswitch_1_sw6,
       dipswitch_1_sw7, dipswitch_1_sw8, dipswitch_2_sw1, dipswitch_2_sw2, dipswitch_2_sw3, dipswitch_2_sw4,
       dipswitch_2_sw5, dipswitch_2_sw6, dipswitch_2_sw7, dipswitch_2_sw8, impl_add16_1_out0,
       impl_add16_1_out1, impl_add16_1_out2, impl_add16_1_out3, impl_add16_1_out4, impl_add16_1_out5,
       impl_add16_1_out6, impl_add16_1_out7, impl_add16_1_ov;

  DipSwitch dipswitch_1 (
    .sw1(dipswitch_1_sw1), .sw2(dipswitch_1_sw2), .sw3(dipswitch_1_sw3), .sw4(dipswitch_1_sw4),
    .sw5(dipswitch_1_sw5), .sw6(dipswitch_1_sw6), .sw7(dipswitch_1_sw7), .sw8(dipswitch_1_sw8));
  DipSwitch dipswitch_2 (
    .sw1(dipswitch_2_sw1), .sw2(dipswitch_2_sw2), .sw3(dipswitch_2_sw3), .sw4(dipswitch_2_sw4),
    .sw5(dipswitch_2_sw5), .sw6(dipswitch_2_sw6), .sw7(dipswitch_2_sw7), .sw8(dipswitch_2_sw8));
  LED led_1 (.in(impl_add16_1_ov));
  Impl_Add16 impl_add16_1 (
    .a7(dipswitch_1_sw1), .b7(dipswitch_2_sw1), .a6(dipswitch_1_sw2), .b6(dipswitch_2_sw2),
    .a5(dipswitch_1_sw3), .b5(dipswitch_2_sw3), .a4(dipswitch_1_sw4), .b4(dipswitch_2_sw4),
    .a3(dipswitch_1_sw5), .b3(dipswitch_2_sw5), .a2(dipswitch_1_sw6), .b2(dipswitch_2_sw6),
    .a1(dipswitch_1_sw7), .b1(dipswitch_2_sw7), .a0(dipswitch_1_sw8), .b0(dipswitch_2_sw8),
    .out7(impl_add16_1_out7), .ov(impl_add16_1_ov), .out6(impl_add16_1_out6), .out5(impl_add16_1_out5),
    .out4(impl_add16_1_out4), .out3(impl_add16_1_out3), .out2(impl_add16_1_out2), .out1(impl_add16_1_out1),
    .out0(impl_add16_1_out0));
  LedBar ledbar_1 (
    .led0(impl_add16_1_out7), .led1(impl_add16_1_out6), .led2(impl_add16_1_out5), .led3(impl_add16_1_out4),
    .led4(impl_add16_1_out3), .led5(impl_add16_1_out2), .led6(impl_add16_1_out1), .led7(impl_add16_1_out0));
endmodule

module Impl_Inc16 (
  input  in_0,
  input  in_1,
  input  in_2,
  input  in_3,
  input  in_4,
  input  in_5,
  input  in_6,
  input  in_7,
  output out_0,
  output out_1,
  output out_2,
  output out_3,
  output out_4,
  output out_5,
  output out_6,
  output out_7,
  output ov
);

  wire impl_halfadder_1_carry, impl_halfadder_2_carry, impl_halfadder_3_carry, impl_halfadder_4_carry,
       impl_halfadder_5_carry, impl_halfadder_6_carry, impl_halfadder_7_carry;

  Impl_HalfAdder impl_halfadder_1 (.a(1'b1), .b(in_0), .sum(out_0), .carry(impl_halfadder_1_carry));
  Impl_HalfAdder impl_halfadder_2 (.a(impl_halfadder_1_carry), .b(in_1), .sum(out_1), .carry(impl_halfadder_2_carry));
  Impl_HalfAdder impl_halfadder_3 (.a(impl_halfadder_2_carry), .b(in_2), .sum(out_2), .carry(impl_halfadder_3_carry));
  Impl_HalfAdder impl_halfadder_4 (.a(impl_halfadder_3_carry), .b(in_3), .sum(out_3), .carry(impl_halfadder_4_carry));
  Impl_HalfAdder impl_halfadder_5 (.a(impl_halfadder_4_carry), .b(in_4), .sum(out_4), .carry(impl_halfadder_5_carry));
  Impl_HalfAdder impl_halfadder_6 (.a(impl_halfadder_5_carry), .b(in_5), .sum(out_5), .carry(impl_halfadder_6_carry));
  Impl_HalfAdder impl_halfadder_7 (.a(impl_halfadder_6_carry), .b(in_6), .sum(out_6), .carry(impl_halfadder_7_carry));
  Impl_HalfAdder impl_halfadder_8 (.a(impl_halfadder_7_carry), .b(in_7), .sum(out_7), .carry(ov));
endmodule

module Impl_ALU (
  input  [15:0] x_16,
  input  zx,
  input  nx,
  input  [15:0] y_16,
  input  zy,
  input  ny,
  input  f,
  input  no,
  output zr,
  output [15:0] out_16,
  output ng
);

  wire lb_8wayor_1_out_2, lb_8wayor_2_out_2, or_1_out;
  wire [15:0] adder_1_out, And16_out, multiplexer_1_out, multiplexer_2_out, multiplexer_3_out,
       multiplexer_4_out, multiplexer_5_out, not_1_out, not_2_out, not_3_out;

  Multiplexer #(.width(16)) multiplexer_1 (.in0(x_16), .in1({16{1'b0}}), .out(multiplexer_1_out), .sel(zx));
  assign not_1_out = ~multiplexer_1_out;  // NOT_Gate not_1, 16 bits wide
  Multiplexer #(.width(16)) multiplexer_2 (.in0(y_16), .in1({16{1'b0}}), .out(multiplexer_2_out), .sel(zy));
  assign not_2_out = ~multiplexer_2_out;  // NOT_Gate not_2, 16 bits wide
  Multiplexer #(.width(16)) multiplexer_3 (.in0(multiplexer_1_out), .in1(not_1_out), .out(multiplexer_3_out), .sel(nx));
  Multiplexer #(.width(16)) multiplexer_4 (.in0(multiplexer_2_out), .in1(not_2_out), .out(multiplexer_4_out), .sel(ny));
  assign And16_out = multiplexer_3_out & multiplexer_4_out;  // AND_Gate And16, 16 bits wide
  Adder #(.width(16)) adder_1 (.a(multiplexer_3_out), .b(multiplexer_4_out), .out(adder_1_out));  // open: cin, cout
  Multiplexer #(.width(16)) multiplexer_5 (.in0(And16_out), .in1(adder_1_out), .out(multiplexer_5_out), .sel(f));
  LB_8WayOr lb_8wayor_1 (.in_1(out_16[7:0]), .out_2(lb_8wayor_1_out_2));
  LB_8WayOr lb_8wayor_2 (.in_1(out_16[15:8]), .out_2(lb_8wayor_2_out_2));
  assign not_3_out = ~multiplexer_5_out;  // NOT_Gate not_3, 16 bits wide
  or or_1 (or_1_out, lb_8wayor_1_out_2, lb_8wayor_2_out_2);
  not not_4 (zr, or_1_out);
  Multiplexer #(.width(16)) multiplexer_6 (.in0(multiplexer_5_out), .in1(not_3_out), .out(out_16), .sel(no));
  BitSelector #(.width(16)) bitselector_1 (.in(out_16), .out(ng), .sel(4'b1111));

  // Notes on the sheet:
  //   16-Bit ALU
endmodule

// 8Or
module LB_8WayOr (
  input  [7:0] in_1,
  output out_2
);

  or or_1 (out_2, in_1[0], in_1[1], in_1[2], in_1[3], in_1[4], in_1[5], in_1[6], in_1[7]);
endmodule
