// Logisim project P3_RAM.circ as structural Verilog
module Bit (
  input  load,
  input  in_1,
  input  clk,
  output out_1
);

  wire multiplexer_1_out;

  D_Flip_Flop d_ff_1 (.D(multiplexer_1_out), .clk(clk), .Q(out_1));  // open: Qn, preset, reset
  Multiplexer multiplexer_1 (.in0(out_1), .in1(in_1), .out(multiplexer_1_out), .sel(load));
endmodule

module Register_8 (
  input  [7:0] in_8,
  input  load,
  input  clk,
  output [7:0] out_8
);

  wire clock_1_out;

  Clock clock_1 (.out(clock_1_out));
  Bit bit_1 (.load(load), .in_1(in_8[0]), .clk(clk), .out_1(out_8[0]));
  Bit bit_2 (.load(load), .in_1(in_8[1]), .clk(clk), .out_1(out_8[1]));
  Bit bit_3 (.load(load), .in_1(in_8[2]), .clk(clk), .out_1(out_8[2]));
  Bit bit_4 (.load(load), .in_1(in_8[3]), .clk(clk), .out_1(out_8[3]));
  Bit bit_5 (.load(load), .in_1(in_8[4]), .clk(clk), .out_1(out_8[4]));
  Bit bit_6 (.load(load), .in_1(in_8[5]), .clk(clk), .out_1(out_8[5]));
  Bit bit_7 (.load(load), .in_1(in_8[6]), .clk(clk), .out_1(out_8[6]));
  Bit bit_8 (.load(load), .in_1(in_8[7]), .clk(clk), .out_1(out_8[7]));
endmodule

module Register_16 (
  input  [15:0] in_16,
  input  load,
  input  clk,
  output [15:0] out_16
);

  wire clock_1_out;

  Clock clock_1 (.out(clock_1_out));
  Register_8 register_8_1 (.in_8(in_16[7:0]), .load(load), .clk(clk), .out_8(out_16[7:0]));
  Register_8 register_8_2 (.in_8(in_16[15:8]), .load(load), .clk(clk), .out_8(out_16[15:8]));
endmodule

module Counter_16 (
  input  [15:0] in_16,
  input  inc,
  input  load,
  input  reset,
  input  clk,
  output [15:0] out_16
);

  wire or_1_out, or_2_out;
  wire [15:0] adder_1_out, multiplexer_1_out, multiplexer_2_out, multiplexer_3_out;

  Adder #(.width(16)) adder_1 (.a(out_16), .b(16'h1), .out(adder_1_out));  // open: cin, cout
  Multiplexer #(.width(16)) multiplexer_1 (.in0(out_16), .in1(adder_1_out), .out(multiplexer_1_out), .sel(inc));
  Multiplexer #(.width(16)) multiplexer_2 (.in0(multiplexer_1_out), .in1(in_16), .out(multiplexer_2_out), .sel(load));
  Multiplexer #(.width(16)) multiplexer_3 (
    .in0(multiplexer_2_out), .in1({16{1'b0}}), .out(multiplexer_3_out), .sel(reset));
  or or_1 (or_1_out, inc, or_2_out);
  or or_2 (or_2_out, load, reset);
  Register_16 register_16_1 (.in_16(multiplexer_3_out), .load(or_1_out), .clk(clk), .out_16(out_16));

  // Notes on the sheet:
  //   Process Counter
endmodule

module Ram8 (
  input  [15:0] in_16,
  input  load,
  input  [2:0] address_3,
  input  clk,
  output [15:0] out_16
);

  wire clock_1_out, demultiplexer_1_out0, demultiplexer_1_out1, demultiplexer_1_out2, demultiplexer_1_out3,
       demultiplexer_1_out4, demultiplexer_1_out5, demultiplexer_1_out6, demultiplexer_1_out7;
  wire [15:0] register_16_1_out_16, register_16_2_out_16, register_16_3_out_16, register_16_4_out_16,
       register_16_5_out_16, register_16_6_out_16, register_16_7_out_16, register_16_8_out_16;

  Clock clock_1 (.out(clock_1_out));
  Demultiplexer #(.select(3)) demultiplexer_1 (
    .out0(demultiplexer_1_out0), .out1(demultiplexer_1_out1), .out2(demultiplexer_1_out2),
    .out3(demultiplexer_1_out3), .out4(demultiplexer_1_out4), .out5(demultiplexer_1_out5),
    .out6(demultiplexer_1_out6), .out7(demultiplexer_1_out7), .in(load), .sel(address_3));
  Register_16 register_16_1 (.in_16(in_16), .load(demultiplexer_1_out0), .clk(clk), .out_16(register_16_1_out_16));
  Register_16 register_16_2 (.in_16(in_16), .load(demultiplexer_1_out1), .clk(clk), .out_16(register_16_2_out_16));
  Register_16 register_16_3 (.in_16(in_16), .load(demultiplexer_1_out2), .clk(clk), .out_16(register_16_3_out_16));
  Register_16 register_16_4 (.in_16(in_16), .load(demultiplexer_1_out3), .clk(clk), .out_16(register_16_4_out_16));
  Register_16 register_16_5 (.in_16(in_16), .load(demultiplexer_1_out4), .clk(clk), .out_16(register_16_5_out_16));
  Register_16 register_16_6 (.in_16(in_16), .load(demultiplexer_1_out5), .clk(clk), .out_16(register_16_6_out_16));
  Register_16 register_16_7 (.in_16(in_16), .load(demultiplexer_1_out6), .clk(clk), .out_16(register_16_7_out_16));
  Register_16 register_16_8 (.in_16(in_16), .load(demultiplexer_1_out7), .clk(clk), .out_16(register_16_8_out_16));
  Multiplexer #(.select(3), .width(16)) multiplexer_1 (
    .in0(register_16_1_out_16), .in1(register_16_2_out_16), .in2(register_16_3_out_16),
    .in3(register_16_4_out_16), .in4(register_16_5_out_16), .in5(register_16_6_out_16),
    .in6(register_16_7_out_16), .in7(register_16_8_out_16), .out(out_16), .sel(address_3));
endmodule

module RAM64 (
  input  [15:0] in_16,
  input  load,
  input  [5:0] address_6,
  input  clk,
  output [15:0] out_16
);

  wire demultiplexer_1_out0, demultiplexer_1_out1, demultiplexer_1_out2, demultiplexer_1_out3,
       demultiplexer_1_out4, demultiplexer_1_out5, demultiplexer_1_out6, demultiplexer_1_out7;
  wire [15:0] ram8_1_out_16, ram8_2_out_16, ram8_3_out_16, ram8_4_out_16, ram8_5_out_16, ram8_6_out_16,
       ram8_7_out_16, ram8_8_out_16;

  Demultiplexer #(.select(3)) demultiplexer_1 (
    .out0(demultiplexer_1_out0), .out1(demultiplexer_1_out1), .out2(demultiplexer_1_out2),
    .out3(demultiplexer_1_out3), .out4(demultiplexer_1_out4), .out5(demultiplexer_1_out5),
    .out6(demultiplexer_1_out6), .out7(demultiplexer_1_out7), .in(load), .sel(address_6[5:3]));
  Ram8 ram8_1 (
    .in_16(in_16), .load(demultiplexer_1_out0), .address_3(address_6[2:0]), .clk(clk), .out_16(ram8_1_out_16));
  Ram8 ram8_2 (
    .in_16(in_16), .load(demultiplexer_1_out1), .address_3(address_6[2:0]), .clk(clk), .out_16(ram8_2_out_16));
  Ram8 ram8_3 (
    .in_16(in_16), .load(demultiplexer_1_out2), .address_3(address_6[2:0]), .clk(clk), .out_16(ram8_3_out_16));
  Ram8 ram8_4 (
    .in_16(in_16), .load(demultiplexer_1_out3), .address_3(address_6[2:0]), .clk(clk), .out_16(ram8_4_out_16));
  Ram8 ram8_5 (
    .in_16(in_16), .load(demultiplexer_1_out4), .address_3(address_6[2:0]), .clk(clk), .out_16(ram8_5_out_16));
  Ram8 ram8_6 (
    .in_16(in_16), .load(demultiplexer_1_out5), .address_3(address_6[2:0]), .clk(clk), .out_16(ram8_6_out_16));
  Ram8 ram8_7 (
    .in_16(in_16), .load(demultiplexer_1_out6), .address_3(address_6[2:0]), .clk(clk), .out_16(ram8_7_out_16));
  Ram8 ram8_8 (
    .in_16(in_16), .load(demultiplexer_1_out7), .address_3(address_6[2:0]), .clk(clk), .out_16(ram8_8_out_16));
  Multiplexer #(.select(3), .width(16)) multiplexer_1 (
    .in0(ram8_1_out_16), .in1(ram8_2_out_16), .in2(ram8_3_out_16), .in3(ram8_4_out_16), .in4(ram8_5_out_16),
    .in5(ram8_6_out_16), .in6(ram8_7_out_16), .in7(ram8_8_out_16), .out(out_16), .sel(address_6[5:3]));

  // Notes on the sheet:
  //   RAM-Modul 64 Byte
endmodule
