// Logisim project P5_Computer.circ as structural Verilog
module CPU2 (
  input  [15:0] instr,
  input  [15:0] inM,
  input  reset,
  input  clk,
  output [15:0] out_5,
  output [15:0] debug_D,
  output [15:0] debug_A,
  output [15:0] out_8,
  output [15:0] outM,
  output writeM,
  output [14:0] addressM,
  output [14:0] PC
);

  wire alu_1_ng, alu_1_zr, bitselector_1_out, bitselector_2_out, Cinst_out, JEQ_out, JGT_out, JLE_out,
       JLT_out, JMP_out, not_1_out, not_2_out, not_3_out, or_1_out, ZN_out;
  wire [2:0] bitselector_5_out;
  wire [2:1] bitselector_4_out;
  wire [5:0] bitselector_3_out;
  wire [15:0] multiplexer_1_out, multiplexer_2_out, multiplexer_3_out, process_counter_1_out_16;

  Multiplexer #(.width(16)) multiplexer_1 (.in0(outM), .in1(instr), .out(multiplexer_1_out), .sel(not_1_out));
  not not_1 (not_1_out, bitselector_1_out);
  BitSelector #(.width(16)) bitselector_1 (.in(instr), .out(bitselector_1_out), .sel(4'b1111));
  Multiplexer #(.width(16)) multiplexer_2 (
    .in0({16{1'b0}}), .in1(instr), .out(multiplexer_2_out), .sel(bitselector_1_out));
  BitSelector #(.width(16)) bitselector_2 (.in(multiplexer_2_out), .out(bitselector_2_out), .sel(4'b1100));
  or or_1 (or_1_out, not_1_out, bitselector_4_out[2]);
  BitSelector #(.group(6), .width(16)) bitselector_3 (.in(multiplexer_2_out), .out(bitselector_3_out), .sel(2'b01));
  BitSelector #(.group(3), .width(16)) bitselector_4 (
    .in(multiplexer_2_out), .out({bitselector_4_out, writeM}), .sel(3'b001));
  BitSelector #(.group(3), .width(16)) bitselector_5 (.in(multiplexer_2_out), .out(bitselector_5_out), .sel(3'b000));
  and JEQ (JEQ_out, alu_1_zr, bitselector_5_out[1]);
  Register_16 A (.in_16(multiplexer_1_out), .load(or_1_out), .clk(clk), .out_16(debug_A));
  or JLE (JLE_out, JEQ_out, JLT_out);
  and JLT (JLT_out, alu_1_ng, bitselector_5_out[2]);
  or ZN (ZN_out, alu_1_ng, alu_1_zr);
  not not_2 (not_2_out, ZN_out);
  Register_16 D (.in_16(outM), .load(bitselector_4_out[1]), .clk(clk), .out_16(debug_D));
  Multiplexer #(.width(16)) multiplexer_3 (.in0(debug_A), .in1(inM), .out(multiplexer_3_out), .sel(bitselector_2_out));
  or JMP (JMP_out, JLE_out, JGT_out);
  and JGT (JGT_out, bitselector_5_out[0], not_2_out);
  and Cinst (Cinst_out, JMP_out, bitselector_1_out);
  not not_3 (not_3_out, Cinst_out);
  ALU alu_1 (
    .x_16(debug_D), .zx(bitselector_3_out[5]), .nx(bitselector_3_out[4]), .y_16(multiplexer_3_out),
    .zy(bitselector_3_out[3]), .ny(bitselector_3_out[2]), .f(bitselector_3_out[1]),
    .no(bitselector_3_out[0]), .zr(alu_1_zr), .out_16(outM), .ng(alu_1_ng));
  Process_Counter process_counter_1 (
    .in_16(debug_A), .inc(not_3_out), .load(Cinst_out), .reset(reset), .clk(clk),
    .out_16(process_counter_1_out_16));
  Reducer15 reducer15_1 (.in_16(debug_A), .out_15(addressM));
  Reducer15 reducer15_2 (.in_16(process_counter_1_out_16), .out_15(PC));

  assign out_5 = debug_D;
  assign out_8 = debug_A;

  // Notes on the sheet:
  //   i=0: A
  //   i=1: C
  //   a=0: Use A 
  //   a=1: Use M
  //   Instruction format: ixxaccccccdddjjj
  //   cccccc: ALU
  //   ddd: Dest
  //   jjj: PC (Jump)
  //   i
  //   cInstr
  //   a
  //   cccccc
  //   ddd
  //   jjj
endmodule

module Impl_OR (
  input  In1,
  input  In2,
  input  in_3,
  input  in_4,
  output Out1,
  output out_6
);

  wire and_1_out, nand_1_out, nand_2_out, not_1_out, not_2_out;

  nand nand_1 (nand_1_out, 1'b1, In1);
  nand nand_2 (nand_2_out, 1'b1, In2);
  not not_1 (not_1_out, in_3);
  not not_2 (not_2_out, in_4);
  and and_1 (and_1_out, not_1_out, not_2_out);
  nand nand_3 (Out1, nand_1_out, nand_2_out);
  not not_3 (out_6, and_1_out);
endmodule

module Impl_XOR (
  input  In1,
  input  In2,
  input  in_3,
  input  in_4,
  output Out1,
  output out_6
);

  wire and_1_out, nand_1_out, nand_2_out, nand_3_out, nand_4_out, not_1_out, or_1_out;

  nand nand_1 (nand_1_out, 1'b1, In1);
  nand nand_2 (nand_2_out, 1'b1, In2);
  or or_1 (or_1_out, in_3, in_4);
  and and_1 (and_1_out, in_3, in_4);
  not not_1 (not_1_out, and_1_out);
  nand nand_3 (nand_3_out, nand_1_out, In2);
  nand nand_4 (nand_4_out, In1, nand_2_out);
  and and_2 (out_6, or_1_out, not_1_out);
  nand nand_5 (Out1, nand_3_out, nand_4_out);
endmodule

module Impl_NOT (
  input  In1,
  output Out1
);

  nand nand_1 (Out1, 1'b1, In1);
endmodule

module Impl_Mux_Demux (
  input  a_m,
  input  b_m,
  input  sel_m,
  input  in_d,
  input  sel_d,
  output out_m,
  output a_d,
  output b_d
);

  wire and_1_out, and_2_out, not_1_out, not_2_out;

  not not_1 (not_1_out, sel_m);
  not not_2 (not_2_out, sel_d);
  and and_1 (and_1_out, not_1_out, a_m);
  and and_2 (and_2_out, b_m, sel_m);
  and and_3 (a_d, not_2_out, in_d);
  and and_4 (b_d, sel_d, in_d);
  or or_1 (out_m, and_1_out, and_2_out);
endmodule

module Impl_Mux4Way16 (
  input  a,
  input  b,
  input  c,
  input  d,
  input  sel_0,
  input  sel_1,
  output out_m16
);

  wire multiplexer_1_out, multiplexer_2_out;

  Multiplexer multiplexer_1 (.in0(a), .in1(b), .out(multiplexer_1_out), .sel(sel_0));
  Multiplexer multiplexer_2 (.in0(c), .in1(d), .out(multiplexer_2_out), .sel(sel_0));
  Multiplexer multiplexer_3 (.in0(multiplexer_1_out), .in1(multiplexer_2_out), .out(out_m16), .sel(sel_1));
endmodule

module Impl_Demux4Way (
  input  d_in,
  input  sel_1,
  input  sel_0,
  output a,
  output b,
  output c,
  output d
);

  wire demultiplexer_2_out0, demultiplexer_2_out1;

  Demultiplexer demultiplexer_1 (.out0(a), .out1(b), .in(demultiplexer_2_out0), .sel(sel_0));
  Demultiplexer demultiplexer_2 (.out0(demultiplexer_2_out0), .out1(demultiplexer_2_out1), .in(d_in), .sel(sel_1));
  Demultiplexer demultiplexer_3 (.out0(c), .out1(d), .in(demultiplexer_2_out1), .sel(sel_0));
endmodule

module Impl_HalfAdder (
  input  a,
  input  b,
  output sum,
  output carry
);

  and and_1 (carry, a, b);
  xor xor_1 (sum, a, b);
endmodule

module Impl_FullAdder (
  input  a,
  input  b,
  input  c,
  input  a1,
  input  b1,
  input  c1,
  output sum,
  output carry,
  output sum1,
  output carry1
);

  wire and_1_out, and_2_out, impl_halfadder_1_carry, impl_halfadder_1_sum, impl_halfadder_2_carry, xor_1_out;

  xor xor_1 (xor_1_out, b, c);
  and and_1 (and_1_out, b, c);
  xor xor_2 (sum, a, xor_1_out);
  and and_2 (and_2_out, a, xor_1_out);
  Impl_HalfAdder impl_halfadder_1 (.a(b1), .b(c1), .sum(impl_halfadder_1_sum), .carry(impl_halfadder_1_carry));
  or or_1 (carry, and_2_out, and_1_out);
  Impl_HalfAdder impl_halfadder_2 (.a(a1), .b(impl_halfadder_1_sum), .sum(sum1), .carry(impl_halfadder_2_carry));
  or or_2 (carry1, impl_halfadder_2_carry, impl_halfadder_1_carry);
endmodule

module Impl_Add16 (
  input  a7,
  input  b7,
  input  a6,
  input  b6,
  input  a5,
  input  b5,
  input  a4,
  input  b4,
  input  a3,
  input  b3,
  input  a2,
  input  b2,
  input  a1,
  input  b1,
  input  a0,
  input  b0,
  output out7,
  output ov,
  output out6,
  output out5,
  output out4,
  output out3,
  output out2,
  output out1,
  output out0
);

  wire impl_fulladder_2_carry, impl_fulladder_3_carry, impl_fulladder_4_carry, impl_fulladder_5_carry,
       impl_fulladder_6_carry, impl_fulladder_7_carry, impl_fulladder_8_carry;

  Impl_FullAdder impl_fulladder_1 (
    .a(a7), .b(b7), .c(impl_fulladder_2_carry), .sum(out7), .carry(ov));  // open: a1, b1, c1, sum1, carry1
  Impl_FullAdder impl_fulladder_2 (
    .a(a6), .b(b6), .c(impl_fulladder_3_carry), .sum(out6), .carry(impl_fulladder_2_carry));  // open: a1, b1, c1, sum1, carry1
  Impl_FullAdder impl_fulladder_3 (
    .a(a5), .b(b5), .c(impl_fulladder_4_carry), .sum(out5), .carry(impl_fulladder_3_carry));  // open: a1, b1, c1, sum1, carry1
  Impl_FullAdder impl_fulladder_4 (
    .a(a4), .b(b4), .c(impl_fulladder_5_carry), .sum(out4), .carry(impl_fulladder_4_carry));  // open: a1, b1, c1, sum1, carry1
  Impl_FullAdder impl_fulladder_5 (
    .a(a3), .b(b3), .c(impl_fulladder_6_carry), .sum(out3), .carry(impl_fulladder_5_carry));  // open: a1, b1, c1, sum1, carry1
  Impl_FullAdder impl_fulladder_6 (
    .a(a2), .b(b2), .c(impl_fulladder_7_carry), .sum(out2), .carry(impl_fulladder_6_carry));  // open: a1, b1, c1, sum1, carry1
  Impl_FullAdder impl_fulladder_7 (
    .a(a1), .b(b1), .c(impl_fulladder_8_carry), .sum(out1), .carry(impl_fulladder_7_carry));  // open: a1, b1, c1, sum1, carry1
  Impl_FullAdder impl_fulladder_8 (
    .a(a0), .b(b0), .c(1'b0), .sum(out0), .carry(impl_fulladder_8_carry));  // open: a1, b1, c1, sum1, carry1
endmodule

module test_Add16 (
);

  wire dipswitch_1_sw1, dipswitch_1_sw2, dipswitch_1_sw3, dipswitch_1_sw4, dipswitch_1_sw5, dipswitch_1_sw6,
       dipswitch_1_sw7, dipswitch_1_sw8, dipswitch_2_sw1, dipswitch_2_sw2, dipswitch_2_sw3, dipswitch_2_sw4,
       dipswitch_2_sw5, dipswitch_2_sw6, dipswitch_2_sw7, dipswitch_2_sw8, impl_add16_1_out0,
       impl_add16_1_out1, impl_add16_1_out2, impl_add16_1_out3, impl_add16_1_out4, impl_add16_1_out5,
       impl_add16_1_out6, impl_add16_1_out7, impl_add16_1_ov;

  DipSwitch dipswitch_1 (
    .sw1(dipswitch_1_sw1), .sw2(dipswitch_1_sw2), .sw3(dipswitch_1_sw3), .sw4(dipswitch_1_sw4),
    .sw5(dipswitch_1_sw5), .sw6(dipswitch_1_sw6), .sw7(dipswitch_1_sw7), .sw8(dipswitch_1_sw8));
  DipSwitch dipswitch_2 (
    .sw1(dipswitch_2_sw1), .sw2(dipswitch_2_sw2), .sw3(dipswitch_2_sw3), .sw4(dipswitch_2_sw4),
    .sw5(dipswitch_2_sw5), .sw6(dipswitch_2_sw6), .sw7(dipswitch_2_sw7), .sw8(dipswitch_2_sw8));
  LED led_1 (.in(impl_add16_1_ov));
  Impl_Add16 impl_add16_1 (
    .a7(dipswitch_1_sw1), .b7(dipswitch_2_sw1), .a6(dipswitch_1_sw2), .b6(dipswitch_2_sw2),
    .a5(dipswitch_1_sw3), .b5(dipswitch_2_sw3), .a4(dipswitch_1_sw4), .b4(dipswitch_2_sw4),
    .a3(dipswitch_1_sw5), .b3(dipswitch_2_sw5), .a2(dipswitch_1_sw6), .b2(dipswitch_2_sw6),
    .a1(dipswitch_1_sw7), .b1(dipswitch_2_sw7), .a0(dipswitch_1_sw8), .b0(dipswitch_2_sw8),
    .out7(impl_add16_1_out7), .ov(impl_add16_1_ov), .out6(impl_add16_1_out6), .out5(impl_add16_1_out5),
    .out4(impl_add16_1_out4), .out3(impl_add16_1_out3), .out2(impl_add16_1_out2), .out1(impl_add16_1_out1),
    .out0(impl_add16_1_out0));
  LedBar ledbar_1 (
    .led0(impl_add16_1_out7), .led1(impl_add16_1_out6), .led2(impl_add16_1_out5), .led3(impl_add16_1_out4),
    .led4(impl_add16_1_out3), .led5(impl_add16_1_out2), .led6(impl_add16_1_out1), .led7(impl_add16_1_out0));
endmodule

module Impl_Inc16 (
  input  in_0,
  input  in_1,
  input  in_2,
  input  in_3,
  input  in_4,
  input  in_5,
  input  in_6,
  input  in_7,
  output out_0,
  output out_1,
  output out_2,
  output out_3,
  output out_4,
  output out_5,
  output out_6,
  output out_7,
  output ov
);

  wire impl_halfadder_1_carry, impl_halfadder_2_carry, impl_halfadder_3_carry, impl_halfadder_4_carry,
       impl_halfadder_5_carry, impl_halfadder_6_carry, impl_halfadder_7_carry;

  Impl_HalfAdder impl_halfadder_1 (.a(1'b1), .b(in_0), .sum(out_0), .carry(impl_halfadder_1_carry));
  Impl_HalfAdder impl_halfadder_2 (.a(impl_halfadder_1_carry), .b(in_1), .sum(out_1), .carry(impl_halfadder_2_carry));
  Impl_HalfAdder impl_halfadder_3 (.a(impl_halfadder_2_carry), .b(in_2), .sum(out_2), .carry(impl_halfadder_3_carry));
  Impl_HalfAdder impl_halfadder_4 (.a(impl_halfadder_3_carry), .b(in_3), .sum(out_3), .carry(impl_halfadder_4_carry));
  Impl_HalfAdder impl_halfadder_5 (.a(impl_halfadder_4_carry), .b(in_4), .sum(out_4), .carry(impl_halfadder_5_carry));
  Impl_HalfAdder impl_halfadder_6 (.a(impl_halfadder_5_carry), .b(in_5), .sum(out_5), .carry(impl_halfadder_6_carry));
  Impl_HalfAdder impl_halfadder_7 (.a(impl_halfadder_6_carry), .b(in_6), .sum(out_6), .carry(impl_halfadder_7_carry));
  Impl_HalfAdder impl_halfadder_8 (.a(impl_halfadder_7_carry), .b(in_7), .sum(out_7), .carry(ov));
endmodule

module ALU (
  input  [15:0] x_16,
  input  zx,
  input  nx,
  input  [15:0] y_16,
  input  zy,
  input  ny,
  input  f,
  input  no,
  output zr,
  output [15:0] out_16,
  output ng
);

  wire lb_8wayor_1_out_2, lb_8wayor_2_out_2, or_1_out;
  wire [15:0] adder_1_out, And16_out, multiplexer_1_out, multiplexer_2_out, multiplexer_3_out,
       multiplexer_4_out, multiplexer_5_out, not_1_out, not_2_out, not_3_out;

  Multiplexer #(.width(16)) multiplexer_1 (.in0(x_16), .in1({16{1'b0}}), .out(multiplexer_1_out), .sel(zx));
  assign not_1_out = ~multiplexer_1_out;  // NOT_Gate not_1, 16 bits wide
  Multiplexer #(.width(16)) multiplexer_2 (.in0(y_16), .in1({16{1'b0}}), .out(multiplexer_2_out), .sel(zy));
  assign not_2_out = ~multiplexer_2_out;  // NOT_Gate not_2, 16 bits wide
  Multiplexer #(.width(16)) multiplexer_3 (.in0(multiplexer_1_out), .in1(not_1_out), .out(multiplexer_3_out), .sel(nx));
  Multiplexer #(.width(16)) multiplexer_4 (.in0(multiplexer_2_out), .in1(not_2_out), .out(multiplexer_4_out), .sel(ny));
  assign And16_out = multiplexer_3_out & multiplexer_4_out;  // AND_Gate And16, 16 bits wide
  Adder #(.width(16)) adder_1 (.a(multiplexer_3_out), .b(multiplexer_4_out), .out(adder_1_out));  // open: cin, cout
  Multiplexer #(.width(16)) multiplexer_5 (.in0(And16_out), .in1(adder_1_out), .out(multiplexer_5_out), .sel(f));
  LB_8WayOr lb_8wayor_1 (.in_1(out_16[7:0]), .out_2(lb_8wayor_1_out_2));
  LB_8WayOr lb_8wayor_2 (.in_1(out_16[15:8]), .out_2(lb_8wayor_2_out_2));
  assign not_3_out = ~multiplexer_5_out;  // NOT_Gate not_3, 16 bits wide
  or or_1 (or_1_out, lb_8wayor_1_out_2, lb_8wayor_2_out_2);
  not not_4 (zr, or_1_out);
  Multiplexer #(.width(16)) multiplexer_6 (.in0(multiplexer_5_out), .in1(not_3_out), .out(out_16), .sel(no));
  BitSelector #(.width(16)) bitselector_1 (.in(out_16), .out(ng), .sel(4'b1111));

  // Notes on the sheet:
  //   16-Bit ALU
endmodule

// 8Or
module LB_8WayOr (
  input  [7:0] in_1,
  output out_2
);

  or or_1 (out_2, in_1[0], in_1[1], in_1[2], in_1[3], in_1[4], in_1[5], in_1[6], in_1[7]);
endmodule

module Bit (
  input  load,
  input  in_1,
  input  clk,
  output out_1
);

  wire multiplexer_1_out;

  D_Flip_Flop d_ff_1 (.D(multiplexer_1_out), .clk(clk), .Q(out_1));  // open: Qn, preset, reset
  Multiplexer multiplexer_1 (.in0(out_1), .in1(in_1), .out(multiplexer_1_out), .sel(load));
endmodule

module Register_8 (
  input  [7:0] in_8,
  input  load,
  input  clk,
  output [7:0] out_8
);

  wire clock_1_out;

  Clock clock_1 (.out(clock_1_out));
  Bit bit_1 (.load(load), .in_1(in_8[0]), .clk(clk), .out_1(out_8[0]));
  Bit bit_2 (.load(load), .in_1(in_8[1]), .clk(clk), .out_1(out_8[1]));
  Bit bit_3 (.load(load), .in_1(in_8[2]), .clk(clk), .out_1(out_8[2]));
  Bit bit_4 (.load(load), .in_1(in_8[3]), .clk(clk), .out_1(out_8[3]));
  Bit bit_5 (.load(load), .in_1(in_8[4]), .clk(clk), .out_1(out_8[4]));
  Bit bit_6 (.load(load), .in_1(in_8[5]), .clk(clk), .out_1(out_8[5]));
  Bit bit_7 (.load(load), .in_1(in_8[6]), .clk(clk), .out_1(out_8[6]));
  Bit bit_8 (.load(load), .in_1(in_8[7]), .clk(clk), .out_1(out_8[7]));
endmodule

module Register_16 (
  input  [15:0] in_16,
  input  load,
  input  clk,
  output [15:0] out_16
);

  wire clock_1_out;

  Clock clock_1 (.out(clock_1_out));
  Register_8 register_8_1 (.in_8(in_16[7:0]), .load(load), .clk(clk), .out_8(out_16[7:0]));
  Register_8 register_8_2 (.in_8(in_16[15:8]), .load(load), .clk(clk), .out_8(out_16[15:8]));
endmodule

module Process_Counter (
  input  [15:0] in_16,
  input  inc,
  input  load,
  input  reset,
  input  clk,
  output [15:0] out_16
);

  wire or_1_out, or_2_out;
  wire [15:0] adder_1_out, multiplexer_1_out, multiplexer_2_out, multiplexer_3_out;

  Adder #(.width(16)) adder_1 (.a(out_16), .b(16'h1), .out(adder_1_out));  // open: cin, cout
  Multiplexer #(.width(16)) multiplexer_1 (.in0(out_16), .in1(adder_1_out), .out(multiplexer_1_out), .sel(inc));
  Multiplexer #(.width(16)) multiplexer_2 (.in0(multiplexer_1_out), .in1(in_16), .out(multiplexer_2_out), .sel(load));
  Multiplexer #(.width(16)) multiplexer_3 (
    .in0(multiplexer_2_out), .in1({16{1'b0}}), .out(multiplexer_3_out), .sel(reset));
  or or_1 (or_1_out, inc, or_2_out);
  or or_2 (or_2_out, load, reset);
  Register_16 register_16_1 (.in_16(multiplexer_3_out), .load(or_1_out), .clk(clk), .out_16(out_16));

  // Notes on the sheet:
  //   Process Counter
endmodule

module Ram8 (
  input  [15:0] in_16,
  input  load,
  input  [2:0] address_3,
  input  clk,
  output [15:0] out_16
);

  wire clock_1_out, demultiplexer_1_out0, demultiplexer_1_out1, demultiplexer_1_out2, demultiplexer_1_out3,
       demultiplexer_1_out4, demultiplexer_1_out5, demultiplexer_1_out6, demultiplexer_1_out7;
  wire [15:0] register_16_1_out_16, register_16_2_out_16, register_16_3_out_16, register_16_4_out_16,
       register_16_5_out_16, register_16_6_out_16, register_16_7_out_16, register_16_8_out_16;

  Clock clock_1 (.out(clock_1_out));
  Demultiplexer #(.select(3)) demultiplexer_1 (
    .out0(demultiplexer_1_out0), .out1(demultiplexer_1_out1), .out2(demultiplexer_1_out2),
    .out3(demultiplexer_1_out3), .out4(demultiplexer_1_out4), .out5(demultiplexer_1_out5),
    .out6(demultiplexer_1_out6), .out7(demultiplexer_1_out7), .in(load), .sel(address_3));
  Register_16 register_16_1 (.in_16(in_16), .load(demultiplexer_1_out0), .clk(clk), .out_16(register_16_1_out_16));
  Register_16 register_16_2 (.in_16(in_16), .load(demultiplexer_1_out1), .clk(clk), .out_16(register_16_2_out_16));
  Register_16 register_16_3 (.in_16(in_16), .load(demultiplexer_1_out2), .clk(clk), .out_16(register_16_3_out_16));
  Register_16 register_16_4 (.in_16(in_16), .load(demultiplexer_1_out3), .clk(clk), .out_16(register_16_4_out_16));
  Register_16 register_16_5 (.in_16(in_16), .load(demultiplexer_1_out4), .clk(clk), .out_16(register_16_5_out_16));
  Register_16 register_16_6 (.in_16(in_16), .load(demultiplexer_1_out5), .clk(clk), .out_16(register_16_6_out_16));
  Register_16 register_16_7 (.in_16(in_16), .load(demultiplexer_1_out6), .clk(clk), .out_16(register_16_7_out_16));
  Register_16 register_16_8 (.in_16(in_16), .load(demultiplexer_1_out7), .clk(clk), .out_16(register_16_8_out_16));
  Multiplexer #(.select(3), .width(16)) multiplexer_1 (
    .in0(register_16_1_out_16), .in1(register_16_2_out_16), .in2(register_16_3_out_16),
    .in3(register_16_4_out_16), .in4(register_16_5_out_16), .in5(register_16_6_out_16),
    .in6(register_16_7_out_16), .in7(register_16_8_out_16), .out(out_16), .sel(address_3));
endmodule

module RAM64 (
  input  [15:0] in_16,
  input  load,
  input  [5:0] address_6,
  input  clk,
  output [15:0] out_16
);

  wire demultiplexer_1_out0, demultiplexer_1_out1, demultiplexer_1_out2, demultiplexer_1_out3,
       demultiplexer_1_out4, demultiplexer_1_out5, demultiplexer_1_out6, demultiplexer_1_out7;
  wire [15:0] ram8_1_out_16, ram8_2_out_16, ram8_3_out_16, ram8_4_out_16, ram8_5_out_16, ram8_6_out_16,
       ram8_7_out_16, ram8_8_out_16;

  Demultiplexer #(.select(3)) demultiplexer_1 (
    .out0(demultiplexer_1_out0), .out1(demultiplexer_1_out1), .out2(demultiplexer_1_out2),
    .out3(demultiplexer_1_out3), .out4(demultiplexer_1_out4), .out5(demultiplexer_1_out5),
    .out6(demultiplexer_1_out6), .out7(demultiplexer_1_out7), .in(load), .sel(address_6[5:3]));
  Ram8 ram8_1 (
    .in_16(in_16), .load(demultiplexer_1_out0), .address_3(address_6[2:0]), .clk(clk), .out_16(ram8_1_out_16));
  Ram8 ram8_2 (
    .in_16(in_16), .load(demultiplexer_1_out1), .address_3(address_6[2:0]), .clk(clk), .out_16(ram8_2_out_16));
  Ram8 ram8_3 (
    .in_16(in_16), .load(demultiplexer_1_out2), .address_3(address_6[2:0]), .clk(clk), .out_16(ram8_3_out_16));
  Ram8 ram8_4 (
    .in_16(in_16), .load(demultiplexer_1_out3), .address_3(address_6[2:0]), .clk(clk), .out_16(ram8_4_out_16));
  Ram8 ram8_5 (
    .in_16(in_16), .load(demultiplexer_1_out4), .address_3(address_6[2:0]), .clk(clk), .out_16(ram8_5_out_16));
  Ram8 ram8_6 (
    .in_16(in_16), .load(demultiplexer_1_out5), .address_3(address_6[2:0]), .clk(clk), .out_16(ram8_6_out_16));
  Ram8 ram8_7 (
    .in_16(in_16), .load(demultiplexer_1_out6), .address_3(address_6[2:0]), .clk(clk), .out_16(ram8_7_out_16));
  Ram8 ram8_8 (
    .in_16(in_16), .load(demultiplexer_1_out7), .address_3(address_6[2:0]), .clk(clk), .out_16(ram8_8_out_16));
  Multiplexer #(.select(3), .width(16)) multiplexer_1 (
    .in0(ram8_1_out_16), .in1(ram8_2_out_16), .in2(ram8_3_out_16), .in3(ram8_4_out_16), .in4(ram8_5_out_16),
    .in5(ram8_6_out_16), .in6(ram8_7_out_16), .in7(ram8_8_out_16), .out(out_16), .sel(address_6[5:3]));

  // Notes on the sheet:
  //   RAM-Modul 64 Byte
endmodule

module CPU (
  input  [15:0] instr,
  input  [15:0] inM,
  input  reset,
  input  clk,
  output [15:0] A_Register,
  output [15:0] D_Register,
  output [15:0] outM,
  output writeM,
  output [14:0] addressM,
  output [14:0] pc
);

  wire alu_1_ng, alu_1_zr, bitselector_1_out, bitselector_5_out, JEQ_out, JGE_out, JGT_out, JLE_out, JLT_out,
       JMP_out, not_1_out, not_2_out, or_1_out, RGT_out;
  wire [2:0] bitselector_4_out;
  wire [2:1] bitselector_3_out;
  wire [5:0] bitselector_2_out;
  wire [15:0] multiplexer_1_out, multiplexer_2_out, multiplexer_3_out, process_counter_1_out_16;

  BitSelector #(.width(16)) bitselector_1 (.in(instr), .out(bitselector_1_out), .sel(4'b1111));
  Multiplexer #(.width(16)) multiplexer_1 (.in0(outM), .in1(instr), .out(multiplexer_1_out), .sel(not_1_out));
  not not_1 (not_1_out, bitselector_1_out);
  Multiplexer #(.width(16)) multiplexer_2 (
    .in0({16{1'b0}}), .in1(instr), .out(multiplexer_2_out), .sel(bitselector_1_out));
  or or_1 (or_1_out, not_1_out, bitselector_3_out[2]);
  BitSelector #(.group(6), .width(16)) bitselector_2 (.in(multiplexer_2_out), .out(bitselector_2_out), .sel(2'b01));
  BitSelector #(.group(3), .width(16)) bitselector_3 (
    .in(multiplexer_2_out), .out({bitselector_3_out, writeM}), .sel(3'b001));
  BitSelector #(.group(3), .width(16)) bitselector_4 (.in(multiplexer_2_out), .out(bitselector_4_out), .sel(3'b000));
  and JEQ (JEQ_out, alu_1_zr, bitselector_4_out[1]);
  and JLT (JLT_out, alu_1_ng, bitselector_4_out[2]);
  Register_16 A (.in_16(multiplexer_1_out), .load(or_1_out), .clk(clk), .out_16(A_Register));
  or JLE (JLE_out, JEQ_out, JLT_out);
  nor RGT (RGT_out, alu_1_zr, alu_1_ng);
  and JGT (JGT_out, RGT_out, bitselector_4_out[0]);
  Multiplexer #(.width(16)) multiplexer_3 (
    .in0(A_Register), .in1(inM), .out(multiplexer_3_out), .sel(bitselector_5_out));
  BitSelector #(.width(16)) bitselector_5 (.in(instr), .out(bitselector_5_out), .sel(4'b1100));
  or JGE (JGE_out, JEQ_out, JGT_out);
  or JMP (JMP_out, JLE_out, JGE_out);
  Register_16 D (.in_16(outM), .load(bitselector_3_out[1]), .clk(clk), .out_16(D_Register));
  not not_2 (not_2_out, JMP_out);
  ALU alu_1 (
    .x_16(D_Register), .zx(bitselector_2_out[5]), .nx(bitselector_2_out[4]), .y_16(multiplexer_3_out),
    .zy(bitselector_2_out[3]), .ny(bitselector_2_out[2]), .f(bitselector_2_out[1]),
    .no(bitselector_2_out[0]), .zr(alu_1_zr), .out_16(outM), .ng(alu_1_ng));
  Process_Counter process_counter_1 (
    .in_16(A_Register), .inc(not_2_out), .load(JMP_out), .reset(reset), .clk(clk),
    .out_16(process_counter_1_out_16));
  Reducer15 reducer15_1 (.in_16(A_Register), .out_15(addressM));
  Reducer15 reducer15_2 (.in_16(process_counter_1_out_16), .out_15(pc));

  // Notes on the sheet:
  //   A/C?
  //   cccccc
  //   ddd
  //   jjj
  //   a?
endmodule

module Reducer15 (
  input  [15:0] in_16,
  output [14:0] out_15
);

  // NoConnect on in_16[15]

  assign out_15 = in_16[14:0];
endmodule
